# Fritzing sketch Keypad (saved by Fritzing 0.9.3b)
breadboards: 1

parts:
  U1 = 2.4" TFT LCD screen, SPI, Touch-enabled
  WeMos_D1_Mini1 = WeMos D1 Mini
  U2 = XD-RF-5V [package=THT]

nets:
  N1: U1.T_IRQ, WeMos_D1_Mini1.D1
  N2: U1.T_DO, U1.SDO, WeMos_D1_Mini1.D6
  N3: U1.T_DIN, U1.SDA, WeMos_D1_Mini1.D7
  N4: U1.T_CS, WeMos_D1_Mini1.D0
  N5: U1.T_CLK, U1.SCL, WeMos_D1_Mini1.D5
  N6: U1.LED, WeMos_D1_Mini1.D3
  N7: U1.DC, WeMos_D1_Mini1.D4
  N8: U1.RESET, WeMos_D1_Mini1.RST
  N9: U1.CS, WeMos_D1_Mini1.D8
  GND: U1.GND, WeMos_D1_Mini1.G, U2.GND
  VCC: U1.VCC, WeMos_D1_Mini1.3V3
  5V: WeMos_D1_Mini1.5V, U2.VCC
  N10: WeMos_D1_Mini1.D2, U2.DATA

custom parts:
  2.4" TFT LCD screen, SPI, Touch-enabled: 2.4", ILI9341-based TFT LCD screen with touch-sensing using the XPT2046 controller, SPI-compatible. There is also an SD-card version that is non-touch enabled but uses exactly the same board and pinout. This part is for both, though it should be noted that the SD reader and the touch screen are mutually incompatible
  XD-RF-5V: This is 433Mhz RF transmitter with receiver kit for Arduino ARM MCU wireless Application environment: Remote control switch, receiver module, motorcycles, automobile anti-theft products, home security products, electric doors, shutter doors, windows, remote control socket, remote control LED, remote audio remote control electric doors, garage door remote control, remote control retractable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
